// Logisim project joc.circ as structural Verilog: 1 circuit, main circuit main
module main (
);

  wire and_5_out, and_6_out, and_7_out, and_8_out, and_9_out, button_1_out, clock_1_out, counter_1_carry,
       counter_3_carry, or_1_out;
  wire [1:0] counter_2_q, random_1_out;
  wire [2:0] counter_3_q;
  wire [3:0] and_1_out, or_2_out, ram_1_data, register_1_q, register_2_q, register_3_q, register_4_q,
       register_5_q, register_6_q, rom_1_data;
  wire [6:0] ram_2_data;

  Clock clock_1 (.out(clock_1_out));
  Random #(.width(2)) random_1 (.clk(clock_1_out), .out(random_1_out));  // open: next, clr
  Counter #(.width(1), .max('h1)) counter_1 (
    .carry(counter_1_carry), .clk(clock_1_out));  // open: load, D, count, Q, clr
  ROM #(.addrWidth(2), .dataWidth(4)) rom_1 (.addr(random_1_out), .data(rom_1_data));  // open: sel
  Button button_1 (.out(button_1_out));
  and and_1 (and_1_out[0], rom_1_data[0], counter_1_carry);
  and and_2 (and_1_out[1], rom_1_data[1], counter_1_carry);
  and and_3 (and_1_out[2], rom_1_data[2], counter_1_carry);
  and and_4 (and_1_out[3], rom_1_data[3], counter_1_carry);
  Counter #(.width(2), .max('h3)) counter_2 (.Q(counter_2_q), .clk(button_1_out));  // open: load, D, count, carry, clr
  Register #(.width(4)) register_1 (
    .D(and_1_out), .Q(register_1_q), .clk(clock_1_out), .clr(counter_3_carry));  // open: en
  Register #(.width(4)) register_2 (
    .D(register_1_q), .Q(register_2_q), .clk(clock_1_out), .clr(counter_3_carry));  // open: en
  Register #(.width(4)) register_3 (
    .D(register_2_q), .Q(register_3_q), .clk(clock_1_out), .clr(counter_3_carry));  // open: en
  Register #(.width(4)) register_4 (
    .D(register_3_q), .Q(register_4_q), .clk(clock_1_out), .clr(counter_3_carry));  // open: en
  Register #(.width(4)) register_5 (
    .D(register_4_q), .Q(register_5_q), .clk(clock_1_out), .clr(counter_3_carry));  // open: en
  Register #(.width(4)) register_6 (
    .D(register_5_q), .Q(register_6_q), .clk(clock_1_out), .clr(counter_3_carry));  // open: en
  RAM #(.addrWidth(2), .dataWidth(4)) ram_1 (.addr(counter_2_q), .data(ram_1_data));  // open: sel, clk, ld, clr
  Counter #(.width(3), .max('h7)) counter_3 (
    .Q(counter_3_q), .carry(counter_3_carry), .clk(or_1_out), .clr(and_6_out));  // open: load, D, count
  and and_5 (and_5_out, register_6_q[3], ram_1_data[3]);
  and and_6 (and_6_out, button_1_out, counter_3_carry);
  or or_1 (or_1_out, and_5_out, and_8_out, and_7_out, and_9_out);
  and and_7 (and_7_out, register_6_q[1], ram_1_data[1]);
  and and_8 (and_8_out, register_6_q[2], ram_1_data[2]);
  DotMatrix #(.inputtype("row"), .matrixcols(4), .matrixrows(5)) dotmatrix_1 (
    .row0(register_1_q), .row1(register_2_q), .row2(register_3_q), .row3(register_4_q), .row4(register_5_q));
  DotMatrix #(.inputtype("row"), .matrixcols(4), .matrixrows(1)) dotmatrix_2 (.row0(or_2_out));
  assign or_2_out = register_6_q | ram_1_data;  // OR_Gate or_2, 4 bits wide
  DotMatrix #(.inputtype("row"), .matrixcols(7), .matrixrows(1)) dotmatrix_3 (.row0(ram_2_data));
  and and_9 (and_9_out, register_6_q[0], ram_1_data[0]);
  RAM #(.addrWidth(3), .dataWidth(7)) ram_2 (.addr(counter_3_q), .data(ram_2_data));  // open: sel, clk, ld, clr

  // Notes on the sheet:
  //   contents of rom_1 (hex, n*v repeats v):
  //   1 2 4 8
endmodule
